// Digital circuit fpga.dig as structural Verilog
module fpga (
  input  push,
  input  [15:0] i,
  input  pop,
  input  we_nostos,
  input  clk,
  input  mux_itos,
  input  mux_ytos,
  output [15:0] ros,
  output [15:0] tos,
  output [11:0] sp,
  output [15:0] nos,
  output [15:0] o
);

  stack stack_1 (
    .clk(clk), .push(push), .pop(pop), .i(i), .y(o), .we_nostos(we_nostos), .we_itos(mux_itos),
    .we_ytos(mux_ytos), .tos(tos), .ros(ros), .nos(nos), .sp(sp));
  Add #(.Bits(16)) add_1 (.a(nos), .b(tos), .c_i(1'b0), .s(o));  // open: c_o

  // Other names for the same wires on the sheet: c = clk
endmodule
